# Fritzing sketch Kiln Controller (saved by Fritzing 0.9.10b)
circuit board: 6.50001cm x 5.65cm
breadboards: 2

parts:
  U2 = Sharp PC817 [package=THT]
  U3 = Sharp PC817 [package=THT]
  U4 = Sharp PC817 [package=THT]
  EMRG = Screw terminal - 2 pins [package=THT]
  CTX = Screw terminal - 2 pins [package=THT]
  HEAT = Screw terminal - 2 pins [package=THT]
  Arduino_Metro_Mini = Adafruit Metro Mini [part_number="Adafruit #2590"]
  U1 = Sharp PC817 [package=THT]
  Q2 = NPN-Transistor [package="SOT-23 [SMD]"]
  DOOR = smd LED [color="Green (570nm)" current=0.030 package="0805 [SMD]"]
  RUN = smd LED [color="Green (570nm)" current=0.030 package="0805 [SMD]"]
  TC-PRI = Screw terminal - 2 pins [package=THT]
  IC2 = SO08-EIAJ [chip_label=MAX31855K package=SO]
  SAFE = smd LED [color="Green (570nm)" current=0.030 package="0805 [SMD]"]
  EMRG_2 = smd LED [color="Green (570nm)" current=0.030 package="0805 [SMD]"]
  DOOR_2 = Screw terminal - 2 pins [package=THT]
  HEAT_2 = smd LED [color="Red (633nm)" current=0.030 package="0805 [SMD]"]
  IC1 = SO08-EIAJ [chip_label=MAX31855K package=SO]
  C2 = Capacitor [mn=0.1uf package=0805]
  C1 = Capacitor [mn=0.1uf package=0805]
  Q1 = NPN-Transistor [package="SOT-23 [SMD]"]
  TC-Safe = Screw terminal - 2 pins [package=THT]
  Raspberry_Pi_1 = Raspberry Pi 3 [part_number=RPI-3-V1.2]
  C4 = Capacitor [mn=10nf package=0603-cap]
  C3 = Capacitor [mn=10nf package=0603-cap]
  R1 = Resistor [tolerance=±5% resistance=47k power=0.25 package="0805 [SMD]"]

nets:
  N1: U2.Pin_1, EMRG.pin1
  N2: U2.Pin_2, EMRG_2.anode
  N3: U2.Pin_4, U3.Pin_3
  N4: U2.Pin_3, U1.Pin_4
  N5: U3.Pin_1, Arduino_Metro_Mini.IO12
  N6: U3.Pin_2, SAFE.anode
  N7: U3.Pin_4, U4.Pin_3
  N8: U4.Pin_1, Raspberry_Pi_1.GPIO9
  N9: U4.Pin_2, RUN.anode
  5V: U4.Pin_4, Arduino_Metro_Mini.VIN, Q2.1, Raspberry_Pi_1.5V
  3.3V: EMRG.pin2, IC2.4, DOOR_2.pin2, IC1.4, C2.2, C1.2, Raspberry_Pi_1.3v3, Raspberry_Pi_1.3V3
  N10: CTX.pin1, Q1.1
  GND: CTX.pin2, HEAT.pin2, Arduino_Metro_Mini.GND, DOOR.cathode, RUN.cathode, IC2.1, SAFE.cathode, EMRG_2.cathode, HEAT_2.cathode, IC1.1, C2.1, C1.1, Q1.2, Raspberry_Pi_1.GND
  N11: HEAT.pin1, Q2.2, HEAT_2.anode
  N12: Arduino_Metro_Mini.AD5/SCL, Raspberry_Pi_1.GPIO3
  N13: Arduino_Metro_Mini.AD4/SDA, Raspberry_Pi_1.GPIO2
  N14: Arduino_Metro_Mini.IO4, IC1.5
  N15: Arduino_Metro_Mini.IO3, IC1.6
  N16: Arduino_Metro_Mini.IO2, IC1.7
  N17: Arduino_Metro_Mini.RESET, Raspberry_Pi_1.GPIO10
  N18: U1.Pin_1, DOOR_2.pin1
  N19: U1.Pin_2, DOOR.anode
  N20: U1.Pin_3, Q1.0
  N21: Q2.0, R1.Pin_1
  N22: TC-PRI.pin1, IC1.2, C4.1
  N23: TC-PRI.pin2, IC1.3, C4.2
  N24: IC2.2, TC-Safe.pin2, C3.1
  N25: IC2.3, TC-Safe.pin1, C3.2
  N26: IC2.5, Raspberry_Pi_1.GPIO22
  N27: IC2.6, Raspberry_Pi_1.GPIO27
  N28: IC2.7, Raspberry_Pi_1.GPIO17
  N29: Raspberry_Pi_1.GPIO11, R1.Pin_0

notes:
  ylw
  red
  Adafruit Metro Mini
  TC-PRI
  TC-SAF
  Kiln Controller
  PiHat v1.1

custom parts:
  Adafruit Metro Mini: We sure love the ATmega328 here at Adafruit, and we use them a lot for our own projects. The processor has plenty of GPIO, Analog inputs, hardware UART SPI and I2C, timers and PWM galore - just enough for most simple projects. When we need to go small, we use a Pro Trinket 3V or 5V, but if you want to have USB-to-Serial built in, we reach for an Adafruit METRO Mini. METRO Mini is the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
